// Logisim project Circuits.circ as structural Verilog: 7 circuits, main circuit RFile
module SCP (
  input  in_1
);

  wire clock_1_out, Ext_Sel, RE, RW, WE;
  wire [1:0] f, PCSrc, Rd_Sel, WBR;
  wire [2:0] B_Sel, imm3L, imm5, Rd_t;
  wire [3:0] ALUOp;
  wire [4:0] Opcode;
  wire [5:3] imm11;
  wire [15:0] ALU_Res, B, imm3L_imm2U__S16, imm5_S16, imm5_Z16, imm5Ext, imm11_S16, imm11_Z16, newPC, PC,
       PC_1, Ra, Rb, Read_Data, Reg_Data, sa_Z16;

  Clock clock_1 (.out(clock_1_out));
  // Probe on newPC
  Register #(.width(16)) u_PC (.D(newPC), .en(1'b1), .Q(PC), .clk(clock_1_out), .clr(in_1));
  // Probe on PC
  // Probe on Opcode
  PC_Control_Unit pc_control_unit_1 (
    .PC(PC), .SignExtend_imm11(imm11_S16), .SignExtend_imm2u_imm3L(imm3L_imm2U__S16),
    .SignExtend_imm5(imm5_S16), .Ra(Ra), .Rb(Rb), .Opcode(Opcode), .PCSrc(PCSrc), .newPC(newPC));
  Main_Control_Unit main_control_unit_1 (
    .Opcode(Opcode), .B_Sel(B_Sel), .ExtendOP(Ext_Sel), .WE(WE), .RE(RE), .WBR(WBR), .Rd_Sel(Rd_Sel),
    .RW(RW), .PCSrc(PCSrc));
  ALU_Control_Unit alu_control_unit_1 (.f(f), .Opcode(Opcode), .ALUop(ALUOp));
  // Probe on f
  // Probe on {f, imm5, imm11, imm3L, Opcode}
  ROM #(.addrWidth(16), .dataWidth(16)) rom_1 (.addr(PC), .data({f, imm5, imm11, imm3L, Opcode}));  // open: sel
  Adder #(.width(16)) adder_1 (.a(PC), .b(16'h1), .out(PC_1));  // open: cin, cout
  // Probe on Rd_t
  // Probe on Reg_Data
  RFile rfile_1 (
    .Data_Out_1(Ra), .Data_Out_2(Rb), .RS1(imm11), .RS2(imm5), .Write_Data(Reg_Data), .Rd(Rd_t), .WE(RW),
    .CLK(clock_1_out), .CLR(clock_1_out));
  // Probe on {f, imm5}
  assign imm5_Z16 = {{11{1'b0}}, {f, imm5}};  // Bit_Extender bit_extender_1
  assign imm5_S16 = {{11{f[1]}}, {f, imm5}};  // Bit_Extender bit_extender_2
  Multiplexer #(.width(16), .enable("false")) multiplexer_1 (
    .in0(imm5_Z16), .in1(imm5_S16), .out(imm5Ext), .sel(Ext_Sel));
  Multiplexer #(.select(2), .width(3), .enable("false")) multiplexer_2 (
    .in0(imm3L), .in1(3'b111), .in2(3'b001), .out(Rd_t), .sel(Rd_Sel));  // open: in3
  Multiplexer #(.select(2), .width(16), .enable("false")) multiplexer_3 (
    .in0(Read_Data), .in1(ALU_Res), .in2(PC_1), .out(Reg_Data), .sel(WBR));  // open: in3
  // Probe on imm5
  // Probe on Ra
  ALU alu_1 (.A(Ra), .B(B), .ALU_Opcode(ALUOp), .ALU_Result(ALU_Res));
  // Probe on B
  // Probe on ALUOp
  assign imm11_Z16 = {{5{1'b0}}, {f, imm5, imm11, imm3L}};  // Bit_Extender bit_extender_3
  assign imm3L_imm2U__S16 = {{11{f[1]}}, {f, imm3L}};  // Bit_Extender bit_extender_4
  assign imm11_S16 = {{5{f[1]}}, {f, imm5, imm11, imm3L}};  // Bit_Extender bit_extender_5
  assign sa_Z16 = {{13{1'b0}}, imm5};  // Bit_Extender bit_extender_6
  // Probe on ALU_Res
  Multiplexer #(.select(3), .width(16), .enable("false")) multiplexer_4 (
    .in0(Rb), .in1(imm5Ext), .in2(imm3L_imm2U__S16), .in3(sa_Z16), .in4(imm11_Z16), .out(B), .sel(B_Sel));  // open: in5, in6, in7
  // Probe on ALU_Res
  // Probe on Rb
  // Probe on Read_Data
  RAM #(.addrWidth(16), .dataWidth(16), .bus("separate")) ram_1 (
    .addr(ALU_Res), .din(Rb), .data(Read_Data), .str(WE), .clk(clock_1_out), .ld(RE));  // open: sel, clr

  // Other names for the same wires on the sheet: imm11 (some bits) = {f, imm5, imm3L}; RD[2:0] = imm3L;
  //   imm2U[1:0] = f; imm5[4:3] = f; RS1[2:0] = imm11; RS2[2:0] = imm5; sa[2:0] = imm5

  // Notes on the sheet:
  //   contents of rom_1 (hex, n*v repeats v):
  //   f8c3 5023 1043 b6 15 0 0 0 e0d fec3 160d fec3 ec3 62c ec3 64c 717 159*0 94c 116c 1a20 5980 9980 19a1
  //   5aa2 59c1 99e1 cc2 8cc2 ccc2 e6e3 c4e4 c4e5 3ce6 3ce7 3ce8 6483 1cc9 1cca 1ccb 756d 7b6e 636f 9*0
  //   6670 10*0 636f 10*0 7473 10*0 6672 10*0 15
endmodule

// Register File
module RFile (
  input  [2:0] RS1,
  input  [2:0] RS2,
  input  [15:0] Write_Data,
  input  [2:0] Rd,
  input  WE,
  input  CLK,
  input  CLR,
  output [15:0] Data_Out_2,
  output [15:0] Data_Out_1
);

  wire and_1_out, and_2_out, and_3_out, and_4_out, and_5_out, and_6_out, and_7_out, decoder_1_out0,
       decoder_1_out1, decoder_1_out2, decoder_1_out3, decoder_1_out4, decoder_1_out5, decoder_1_out6,
       decoder_1_out7, decoder_2_out0, decoder_2_out1, decoder_2_out2, decoder_2_out3, decoder_2_out4,
       decoder_2_out5, decoder_2_out6, decoder_2_out7, decoder_3_out0, decoder_3_out1, decoder_3_out2,
       decoder_3_out3, decoder_3_out4, decoder_3_out5, decoder_3_out6, decoder_3_out7, undriven;
  wire [15:0] register_1_q, register_2_q, register_3_q, register_4_q, register_5_q, register_6_q,
       register_7_q;

  Decoder #(.select(3), .enable("false")) decoder_1 (
    .out0(decoder_1_out0), .out1(decoder_1_out1), .out2(decoder_1_out2), .out3(decoder_1_out3),
    .out4(decoder_1_out4), .out5(decoder_1_out5), .out6(decoder_1_out6), .out7(decoder_1_out7), .sel(Rd));
  and and_1 (and_1_out, decoder_1_out1, WE);
  and and_2 (and_2_out, decoder_1_out2, WE);
  and and_3 (and_3_out, decoder_1_out3, WE);
  and and_4 (and_4_out, decoder_1_out4, WE);
  and and_5 (and_5_out, decoder_1_out5, WE);
  and and_6 (and_6_out, decoder_1_out6, WE);
  and and_7 (and_7_out, decoder_1_out7, WE);
  Decoder #(.select(3), .enable("false")) decoder_2 (
    .out0(decoder_2_out0), .out1(decoder_2_out1), .out2(decoder_2_out2), .out3(decoder_2_out3),
    .out4(decoder_2_out4), .out5(decoder_2_out5), .out6(decoder_2_out6), .out7(decoder_2_out7), .sel(RS1));
  assign Data_Out_1 = decoder_2_out0 ? {16{1'b0}} : 16'bz;  // Controlled_Buffer controlled_buffer_1
  assign Data_Out_1 = decoder_2_out1 ? register_1_q : 16'bz;  // Controlled_Buffer controlled_buffer_2
  Register #(.width(16)) register_1 (.D(Write_Data), .en(and_1_out), .Q(register_1_q), .clk(CLK), .clr(undriven));
  Register #(.width(16)) register_2 (.D(Write_Data), .en(and_2_out), .Q(register_2_q), .clk(CLK), .clr(undriven));
  assign Data_Out_1 = decoder_2_out2 ? register_2_q : 16'bz;  // Controlled_Buffer controlled_buffer_3
  Register #(.width(16)) register_3 (.D(Write_Data), .en(and_3_out), .Q(register_3_q), .clk(CLK), .clr(undriven));
  assign Data_Out_1 = decoder_2_out3 ? register_3_q : 16'bz;  // Controlled_Buffer controlled_buffer_4
  Register #(.width(16)) register_4 (.D(Write_Data), .en(and_4_out), .Q(register_4_q), .clk(CLK), .clr(undriven));
  assign Data_Out_1 = decoder_2_out4 ? register_4_q : 16'bz;  // Controlled_Buffer controlled_buffer_5
  assign Data_Out_1 = decoder_2_out5 ? register_5_q : 16'bz;  // Controlled_Buffer controlled_buffer_6
  Register #(.width(16)) register_5 (.D(Write_Data), .en(and_5_out), .Q(register_5_q), .clk(CLK), .clr(undriven));
  Register #(.width(16)) register_6 (.D(Write_Data), .en(and_6_out), .Q(register_6_q), .clk(CLK), .clr(undriven));
  assign Data_Out_1 = decoder_2_out6 ? register_6_q : 16'bz;  // Controlled_Buffer controlled_buffer_7
  assign Data_Out_1 = decoder_2_out7 ? register_7_q : 16'bz;  // Controlled_Buffer controlled_buffer_8
  Register #(.width(16)) register_7 (.D(Write_Data), .en(and_7_out), .Q(register_7_q), .clk(CLK), .clr(undriven));
  assign Data_Out_2 = decoder_3_out0 ? {16{1'b0}} : 16'bz;  // Controlled_Buffer controlled_buffer_9
  assign Data_Out_2 = decoder_3_out1 ? register_1_q : 16'bz;  // Controlled_Buffer controlled_buffer_10
  assign Data_Out_2 = decoder_3_out2 ? register_2_q : 16'bz;  // Controlled_Buffer controlled_buffer_11
  assign Data_Out_2 = decoder_3_out3 ? register_3_q : 16'bz;  // Controlled_Buffer controlled_buffer_12
  assign Data_Out_2 = decoder_3_out4 ? register_4_q : 16'bz;  // Controlled_Buffer controlled_buffer_13
  assign Data_Out_2 = decoder_3_out5 ? register_5_q : 16'bz;  // Controlled_Buffer controlled_buffer_14
  assign Data_Out_2 = decoder_3_out6 ? register_6_q : 16'bz;  // Controlled_Buffer controlled_buffer_15
  assign Data_Out_2 = decoder_3_out7 ? register_7_q : 16'bz;  // Controlled_Buffer controlled_buffer_16
  Decoder #(.select(3), .enable("false")) decoder_3 (
    .out0(decoder_3_out0), .out1(decoder_3_out1), .out2(decoder_3_out2), .out3(decoder_3_out3),
    .out4(decoder_3_out4), .out5(decoder_3_out5), .out6(decoder_3_out6), .out7(decoder_3_out7), .sel(RS2));
  // Probe on register_1_q
  // Probe on register_2_q
  // Probe on register_3_q
  // Probe on register_4_q
  // Probe on register_5_q
  // Probe on register_6_q
  // Probe on register_7_q
  // also tied to GND on the sheet: decoder_1_out0
endmodule

module ALU (
  input  [15:0] A,
  input  [15:0] B,
  input  [3:0] ALU_Opcode,
  output [15:0] ALU_Result
);

  wire comparator_1_lt, comparator_2_lt;
  wire [15:0] adder_1_out, and_1_out, multiplexer_1_out, multiplexer_2_out, or_1_out, shifter_1_out,
       shifter_2_out, shifter_3_out, shifter_4_out, subtractor_1_out, xor_1_out;

  // Probe on A
  // Probe on B
  Adder #(.width(16)) adder_1 (.a(B), .b(A), .out(adder_1_out));  // open: cin, cout
  Subtractor #(.width(16)) subtractor_1 (.a(A), .b(B), .out(subtractor_1_out));  // open: bin, bout
  Comparator #(.width(16)) comparator_1 (.a(A), .b(B), .lt(comparator_1_lt));  // open: gt, eq
  Comparator #(.width(16), .mode("unsigned")) comparator_2 (.a(A), .b(B), .lt(comparator_2_lt));  // open: gt, eq
  assign xor_1_out = B ^ A;  // XOR_Gate xor_1, 16 bits wide
  assign or_1_out = B | A;  // OR_Gate or_1, 16 bits wide
  assign and_1_out = A & B;  // AND_Gate and_1, 16 bits wide
  Shifter #(.width(16)) shifter_1 (.in(A), .\dist (B[3:0]), .out(shifter_1_out));
  Shifter #(.width(16), .shift("lr")) shifter_2 (.in(A), .\dist (B[3:0]), .out(shifter_2_out));
  Shifter #(.width(16), .shift("ar")) shifter_3 (.in(A), .\dist (B[3:0]), .out(shifter_3_out));
  Shifter #(.width(16)) shifter_4 (.in(B), .\dist (4'b0101), .out(shifter_4_out));
  Multiplexer #(.width(16), .enable("false")) multiplexer_1 (
    .in0({16{1'b0}}), .in1(16'h1), .out(multiplexer_1_out), .sel(comparator_1_lt));
  Multiplexer #(.width(16), .enable("false")) multiplexer_2 (
    .in0({16{1'b0}}), .in1(16'h1), .out(multiplexer_2_out), .sel(comparator_2_lt));
  Multiplexer #(.select(4), .width(16), .enable("false")) multiplexer_3 (
    .in0(adder_1_out), .in1(subtractor_1_out), .in2(multiplexer_1_out), .in3(multiplexer_2_out),
    .in4(xor_1_out), .in5(or_1_out), .in6(and_1_out), .in7(shifter_1_out), .in8(shifter_2_out),
    .in9(shifter_3_out), .in10(shifter_4_out), .out(ALU_Result), .sel(ALU_Opcode));  // open: in11, in12, in13, in14, in15
  // Probe on ALU_Result

  // Notes on the sheet:
  //   ADD
  //   SUB
  //   XOR
  //   OR
  //   AND
  //   SLL
  //   SRL
  //   SRA
  //   SLT
  //   SLTU
endmodule

module ALU_Control_Unit (
  input  [1:0] f,
  input  [4:0] Opcode,
  output [3:0] ALUop
);

  ROM #(.addrWidth(7), .dataWidth(4)) rom_1 (.addr({Opcode, f}), .data(ALUop));  // open: sel

  // Notes on the sheet:
  //   contents of rom_1 (hex, n*v repeats v):
  //   4 5 6 0 7 8 9 0 0 1 2 3 4*0 4*2 4*3 4*4 4*5 4*6 4*7 4*8 4*9 32*0 4*a
endmodule

module Main_Control_Unit (
  input  [4:0] Opcode,
  output [2:0] B_Sel,
  output ExtendOP,
  output WE,
  output RE,
  output [1:0] WBR,
  output [1:0] Rd_Sel,
  output RW,
  output [1:0] PCSrc
);

  ROM #(.addrWidth(5), .dataWidth(11)) rom_1 (
    .addr(Opcode), .data({RW, Rd_Sel, WBR, RE, WE, ExtendOP, B_Sel}));  // open: sel
  ROM #(.addrWidth(5), .dataWidth(2)) rom_2 (.addr(Opcode), .data(PCSrc));  // open: sel

  // Notes on the sheet:
  //   contents of rom_1 (hex, n*v repeats v):
  //   440 440 440 449 449 449 441 441 441 443 443 443 429 3d2 6*3c2 644 3c4 584 481
  //   contents of rom_2 (hex, n*v repeats v):
  //   14*0 6*1 0 2 2 3
endmodule

module PC_Control_Unit (
  input  [15:0] PC,
  input  [15:0] SignExtend_imm11,
  input  [1:0] PCSrc,
  input  [4:0] Opcode,
  input  [15:0] SignExtend_imm2u_imm3L,
  input  [15:0] Ra,
  input  [15:0] Rb,
  input  [15:0] SignExtend_imm5,
  output [15:0] newPC
);

  wire CMP;
  wire [15:0] multiplexer_1_out, PC_1, PC_sign_extend__imm2U__imm3L, PC_sign_extend_imm11,
       Ra_sign_extend_imm5;

  Multiplexer #(.width(16), .enable("false")) multiplexer_1 (
    .in0(PC_1), .in1(PC_sign_extend__imm2U__imm3L), .out(multiplexer_1_out), .sel(CMP));
  Multiplexer #(.select(2), .width(16), .enable("false")) multiplexer_2 (
    .in0(PC_1), .in1(multiplexer_1_out), .in2(PC_sign_extend_imm11), .in3(Ra_sign_extend_imm5), .out(newPC),
    .sel(PCSrc));
  CMP cmp_1 (.Ra(Ra), .Rb(Rb), .CMP(CMP), .Opcode(Opcode));
  Adder #(.width(16)) adder_1 (.a(PC), .b(SignExtend_imm11), .out(PC_sign_extend_imm11));  // open: cin, cout
  Adder #(.width(16)) adder_2 (
    .a(PC), .b(SignExtend_imm2u_imm3L), .out(PC_sign_extend__imm2U__imm3L));  // open: cin, cout
  Adder #(.width(16)) adder_3 (.a(Ra), .b(SignExtend_imm5), .out(Ra_sign_extend_imm5));  // open: cin, cout
  Adder #(.width(16)) adder_4 (.a(PC), .b(16'h1), .out(PC_1));  // open: cin, cout
endmodule

module CMP (
  input  [15:0] Ra,
  input  [15:0] Rb,
  input  [4:0] Opcode,
  output CMP
);

  wire comparator_2_eq, comparator_2_gt, EQ, GE, GEU, GT, LT, LTU, NE;

  Comparator #(.width(16)) comparator_1 (.a(Ra), .b(Rb), .gt(GT), .eq(EQ), .lt(LT));
  Comparator #(.width(16), .mode("unsigned")) comparator_2 (
    .a(Ra), .b(Rb), .gt(comparator_2_gt), .eq(comparator_2_eq), .lt(LTU));
  not not_1 (NE, EQ);
  or or_1 (GE, GT, EQ);
  or or_2 (GEU, comparator_2_gt, comparator_2_eq);
  Multiplexer #(.select(5), .enable("false")) multiplexer_1 (
    .in0(1'b0), .in1(1'b0), .in2(1'b0), .in3(1'b0), .in4(1'b0), .in5(1'b0), .in6(1'b0), .in7(1'b0),
    .in8(1'b0), .in9(1'b0), .in10(1'b0), .in11(1'b0), .in12(1'b0), .in13(1'b0), .in14(EQ), .in15(NE),
    .in16(LT), .in17(GE), .in18(LTU), .in19(GEU), .in20(1'b0), .in21(1'b0), .in22(1'b0), .in23(1'b0),
    .in24(1'b0), .in25(1'b0), .in26(1'b0), .in27(1'b0), .in28(1'b0), .in29(1'b0), .in30(1'b0), .in31(1'b0),
    .out(CMP), .sel(Opcode));
endmodule
